// Logisim project 1001序列检测.circ as structural Verilog: 4 circuits, main circuit main
module main (
);

  wire clk, d_ff_1_q, detecter_1_out_4, not_1_out, random_1_out, rst, shift_register_1_out;

  Clock #(.highDuration(1), .lowDuration(1)) clock_1 (.out(clk));
  Button button_1 (.out(rst));
  Random #(.width(1), .seed(0), .trigger("rising")) random_1 (.clk(clk), .next(1'b1), .out(random_1_out), .clr(rst));
  Shift_Register #(.width(1), .length(32), .parallel("true"), .trigger("rising")) shift_register_1 (
    .shift(1'b1), .in(random_1_out), .clk(clk), .out(shift_register_1_out), .load(1'b0), .clr(rst));  // open: d0, q0, d1, q1, d2, q2, d3, q3, d4, q4, d5, q5, d6, q6, d7, q7, d8, q8, d9, q9, d10, q10, d11, q11, d12, q12, d13, q13, d14, q14, d15, q15, d16, q16, d17, q17, d18, q18, d19, q19, d20, q20, d21, q21, d22, q22, d23, q23, d24, q24, d25, q25, d26, q26, d27, q27, d28, q28, d29, q29, d30, q30, d31, q31
  not not_1 (not_1_out, clk);
  D_Flip_Flop #(.trigger("rising"), .Pre_Clr_Positions("LEGACY"), .NegatePresetClear("false"), .enable("false"), .NewFFLayout("false")) d_ff_1 (
    .clk(not_1_out), .D(shift_register_1_out), .Q(d_ff_1_q));  // open: Qn, preset, reset
  detecter detecter_1 (.clk(clk), .\input (d_ff_1_q), .reset(rst), .out_4(detecter_1_out_4));
  Shift_Register #(.width(1), .length(32), .parallel("true"), .trigger("rising")) shift_register_2 (
    .shift(1'b1), .in(d_ff_1_q), .clk(clk), .load(1'b0), .clr(rst));  // open: out, d0, q0, d1, q1, d2, q2, d3, q3, d4, q4, d5, q5, d6, q6, d7, q7, d8, q8, d9, q9, d10, q10, d11, q11, d12, q12, d13, q13, d14, q14, d15, q15, d16, q16, d17, q17, d18, q18, d19, q19, d20, q20, d21, q21, d22, q22, d23, q23, d24, q24, d25, q25, d26, q26, d27, q27, d28, q28, d29, q29, d30, q30, d31, q31
  Shift_Register #(.width(1), .length(32), .parallel("true"), .trigger("rising")) shift_register_3 (
    .shift(1'b1), .in(detecter_1_out_4), .clk(clk), .load(1'b0), .clr(rst));  // open: out, d0, q0, d1, q1, d2, q2, d3, q3, d4, q4, d5, q5, d6, q6, d7, q7, d8, q8, d9, q9, d10, q10, d11, q11, d12, q12, d13, q13, d14, q14, d15, q15, d16, q16, d17, q17, d18, q18, d19, q19, d20, q20, d21, q21, d22, q22, d23, q23, d24, q24, d25, q25, d26, q26, d27, q27, d28, q28, d29, q29, d30, q30, d31, q31

  // Notes on the sheet:
  //   为了防止状态机接收到的上级输入不稳定（不同步），将寄存器改为时钟下降沿，这样寄存器输出的值在时钟上升沿一定不会改变，序列检测器得到稳定的输入。
endmodule

module status_machine (
  input  \input ,
  input  S0,
  input  S1,
  input  S2,
  input  reset,
  output N0,
  output N1,
  output N2
);

  wire and_1_out, and_2_out, and_3_out, and_4_out, and_5_out, and_6_out, and_7_out, not_1_out, not_2_out,
       not_3_out, not_4_out, not_5_out, not_6_out, not_7_out, not_8_out, not_9_out, not_10_out, not_11_out,
       not_12_out, not_13_out, not_14_out, not_15_out, not_16_out, not_17_out, not_18_out, not_19_out,
       not_20_out, not_21_out, not_22_out, not_23_out, not_24_out, not_25_out, not_26_out, not_27_out,
       not_28_out;

  not not_1 (not_1_out, S2);
  not not_2 (not_2_out, S1);
  not not_3 (not_3_out, S0);
  not not_4 (not_4_out, reset);
  not not_5 (not_5_out, S2);
  not not_6 (not_6_out, S1);
  not not_7 (not_7_out, reset);
  not not_8 (not_8_out, S2);
  not not_9 (not_9_out, S0);
  not not_10 (not_10_out, \input );
  not not_11 (not_11_out, reset);
  not not_12 (not_12_out, S1);
  not not_13 (not_13_out, S0);
  not not_14 (not_14_out, reset);
  not not_15 (not_15_out, S2);
  not not_16 (not_16_out, S1);
  not not_17 (not_17_out, \input );
  not not_18 (not_18_out, reset);
  not not_19 (not_19_out, S2);
  not not_20 (not_20_out, S0);
  not not_21 (not_21_out, \input );
  not not_22 (not_22_out, reset);
  not not_23 (not_23_out, S1);
  not not_24 (not_24_out, S0);
  not not_25 (not_25_out, \input );
  not not_26 (not_26_out, reset);
  not not_27 (not_27_out, S2);
  not not_28 (not_28_out, reset);
  and and_1 (and_1_out, not_1_out, not_2_out, not_3_out, \input , not_4_out);
  and and_2 (and_2_out, not_5_out, not_6_out, S0, \input , not_7_out);
  and and_3 (and_3_out, not_8_out, S1, not_9_out, not_10_out, not_11_out);
  and and_4 (and_4_out, S2, not_12_out, not_13_out, \input , not_14_out);
  and and_5 (and_5_out, not_15_out, not_16_out, S0, not_17_out, not_18_out);
  and and_6 (and_6_out, not_19_out, S1, not_20_out, not_21_out, not_22_out);
  and and_7 (and_7_out, S2, not_23_out, not_24_out, not_25_out, not_26_out);
  and and_8 (N2, not_27_out, S1, S0, \input , not_28_out);
  or or_1 (N0, and_1_out, and_2_out, and_3_out, and_4_out);
  or or_2 (N1, and_5_out, and_6_out, and_7_out);
endmodule

module outputfun (
  input  S0,
  input  S1,
  input  S2,
  output \output 
);

  wire not_1_out, not_2_out;

  not not_1 (not_1_out, S1);
  not not_2 (not_2_out, S0);
  and and_1 (\output , S2, not_1_out, not_2_out);
endmodule

module detecter (
  input  clk,
  input  \input ,
  input  reset,
  output out_4
);

  wire N0, N1, N2, S0, S1, S2;

  D_Flip_Flop #(.trigger("rising"), .Pre_Clr_Positions("LEGACY"), .NegatePresetClear("false"), .enable("false"), .NewFFLayout("false")) d_ff_1 (
    .clk(clk), .D(N0), .Q(S0));  // open: Qn, preset, reset
  status_machine status_machine_1 (
    .\input (\input ), .S0(S0), .S1(S1), .S2(S2), .reset(reset), .N0(N0), .N1(N1), .N2(N2));
  D_Flip_Flop #(.trigger("rising"), .Pre_Clr_Positions("LEGACY"), .NegatePresetClear("false"), .enable("false"), .NewFFLayout("false")) d_ff_2 (
    .clk(clk), .D(N1), .Q(S1));  // open: Qn, preset, reset
  outputfun outputfun_1 (.S0(N0), .S1(N1), .S2(N2), .\output (out_4));
  D_Flip_Flop #(.trigger("rising"), .Pre_Clr_Positions("LEGACY"), .NegatePresetClear("false"), .enable("false"), .NewFFLayout("false")) d_ff_3 (
    .clk(clk), .D(N2), .Q(S2));  // open: Qn, preset, reset

  // Notes on the sheet:
  //   这里的输出由次态激励以避免检测出现1clk的延迟
endmodule
